// Logisim project jrmips-MAS583.circ as structural Verilog: 15 circuits, main circuit main
module main (
);

  wire and_1_out, branch_handler_1_zero_output, clock_1_out, instruction_fields_1_subop,
       main_control_1_alusrc, main_control_1_extendtype, main_control_1_mem2reg, main_control_1_memread,
       main_control_1_memwrite, master_control_1_setregvalue, master_control_1_setregvalue2,
       master_control_1_setregvalue3, master_control_1_writeen, output_control_1_halt, output_control_1_put,
       pc_control_1_branch, pc_control_1_jump, shift_control_1_direction, shift_control_1_rtorshamt;
  wire [1:0] main_control_1_operation, master_control_1_operation, pc_control_1_comparison,
       pc_control_1_jump_type;
  wire [2:0] instruction_fields_1_rs, instruction_fields_1_rt;
  wire [3:0] demultiplexer_1_out0, demultiplexer_1_out1, demultiplexer_1_out2, demultiplexer_1_out3,
       instruction_fields_1_opcode, instruction_fields_1_shamt, register_2_q, register_2_q_2, register_2_q_3,
       register_2_q_4;
  wire [7:0] adder_1_out, data_address_handler_1_effective_address, instruction_fields_1_immediate,
       jump_handler_1_pc_value, multiplexer_3_out, multiplexer_7_out, n16_to_8_bits_1_output,
       n16_to_8_bits_2_output, register_1_q;
  wire [15:0] alu_1_result, bit_extender_1_out, bit_extender_2_out, jump_handler_1_rs_value,
       multiplexer_1_out, multiplexer_2_out, multiplexer_4_out, multiplexer_5_out, multiplexer_6_out,
       multiplexer_8_out, ram_1_data, register_file_1_read_data_0, register_file_1_read_data_1, rom_1_data,
       shift_handler_1_output;

  Clock clock_1 (.out(clock_1_out));
  LED #(.active("false")) Halt (.in(output_control_1_halt));
  Adder adder_1 (.a(8'h1), .b(register_1_q), .out(adder_1_out));  // open: cin, cout
  Register register_1 (
    .D(multiplexer_7_out), .en(output_control_1_halt), .Q(register_1_q), .clk(clock_1_out));  // open: clr
  Shift_handler shift_handler_1 (
    .Shamt(instruction_fields_1_shamt), .Rt(register_file_1_read_data_1),
    .Rt_or_Shamt(shift_control_1_rtorshamt), .Direction(shift_control_1_direction),
    .Input(register_file_1_read_data_0), .Output(shift_handler_1_output));
  Main_Control main_control_1 (
    .Opcode(demultiplexer_1_out1), .SubOp(instruction_fields_1_subop), .AluSrc(main_control_1_alusrc),
    .Operation(main_control_1_operation), .Mem2Reg(main_control_1_mem2reg),
    .ExtendType(main_control_1_extendtype), .MemRead(main_control_1_memread),
    .MemWrite(main_control_1_memwrite));
  Output_Control output_control_1 (
    .Opcode(demultiplexer_1_out0), .Halt(output_control_1_halt), .Put(output_control_1_put));
  Hex_Digit_Display hex_digit_display_1 (.value(register_2_q_4));  // open: dp
  Hex_Digit_Display hex_digit_display_2 (.value(register_2_q_3));  // open: dp
  Hex_Digit_Display hex_digit_display_3 (.value(register_2_q_2));  // open: dp
  ROM #(.dataWidth(16)) rom_1 (.addr(register_1_q), .data(rom_1_data));  // open: sel
  RAM #(.dataWidth(16), .bus("separate")) ram_1 (
    .addr(data_address_handler_1_effective_address), .din(register_file_1_read_data_0), .data(ram_1_data),
    .str(main_control_1_memwrite), .sel(1'b1), .clk(clock_1_out), .ld(main_control_1_memread), .clr(1'b0));
  Hex_Digit_Display hex_digit_display_4 (.value(register_2_q));  // open: dp
  Instruction_Fields instruction_fields_1 (
    .Instruction(rom_1_data), .SubOp(instruction_fields_1_subop), .shamt(instruction_fields_1_shamt),
    .Rt(instruction_fields_1_rt), .Immediate(instruction_fields_1_immediate), .Rs(instruction_fields_1_rs),
    .Opcode(instruction_fields_1_opcode));
  Shift_Control shift_control_1 (
    .Opcode(demultiplexer_1_out2), .SubOp(instruction_fields_1_subop), .Direction(shift_control_1_direction),
    .RtOrShamt(shift_control_1_rtorshamt));
  Multiplexer #(.width(16), .enable("false")) multiplexer_1 (
    .in0(alu_1_result), .in1(ram_1_data), .out(multiplexer_1_out), .sel(main_control_1_mem2reg));
  assign bit_extender_1_out = {{8{1'b0}}, instruction_fields_1_immediate};  // Bit_Extender bit_extender_1
  assign bit_extender_2_out = {{8{instruction_fields_1_immediate[7]}}, instruction_fields_1_immediate};  // Bit_Extender bit_extender_2
  Multiplexer #(.width(16), .enable("false")) multiplexer_2 (
    .in0(shift_handler_1_output), .in1(multiplexer_1_out), .out(multiplexer_2_out),
    .sel(master_control_1_setregvalue));
  Multiplexer #(.width(8), .enable("false")) multiplexer_3 (
    .in0(adder_1_out), .in1(n16_to_8_bits_1_output), .out(multiplexer_3_out), .sel(and_1_out));
  and and_1 (and_1_out, pc_control_1_branch, branch_handler_1_zero_output);
  Multiplexer #(.width(16), .enable("false")) multiplexer_4 (
    .in0(bit_extender_1_out), .in1(bit_extender_2_out), .out(multiplexer_4_out),
    .sel(main_control_1_extendtype));
  Multiplexer #(.width(16), .enable("false")) multiplexer_5 (
    .in0(multiplexer_2_out), .in1(register_file_1_read_data_1), .out(multiplexer_5_out),
    .sel(master_control_1_setregvalue2));
  _16_to_8_bits u_16_to_8_bits_1 (.\input (bit_extender_1_out), .Output(n16_to_8_bits_1_output));
  Branch_Handler branch_handler_1 (
    .RS(n16_to_8_bits_2_output), .Comparison(pc_control_1_comparison),
    .Zero_Output(branch_handler_1_zero_output));
  _16_to_8_bits u_16_to_8_bits_2 (.\input (register_file_1_read_data_0), .Output(n16_to_8_bits_2_output));
  Register_File register_file_1 (
    .Read_Register_0(instruction_fields_1_rs), .Read_Register_1(instruction_fields_1_rt),
    .Clock(clock_1_out), .Write_Enable(master_control_1_writeen), .Write_Data(multiplexer_6_out),
    .Write_Register(instruction_fields_1_rs), .Read_Data_0(register_file_1_read_data_0),
    .Read_Data_1(register_file_1_read_data_1));
  Multiplexer #(.width(16), .enable("false")) multiplexer_6 (
    .in0(multiplexer_5_out), .in1(jump_handler_1_rs_value), .out(multiplexer_6_out),
    .sel(master_control_1_setregvalue3));
  Multiplexer #(.width(8), .enable("false")) multiplexer_7 (
    .in0(multiplexer_3_out), .in1(jump_handler_1_pc_value), .out(multiplexer_7_out), .sel(pc_control_1_jump));
  PC_Control pc_control_1 (
    .Opcode(demultiplexer_1_out3), .Comparison(pc_control_1_comparison), .Branch(pc_control_1_branch),
    .Jump(pc_control_1_jump), .Jump_Type(pc_control_1_jump_type));
  Master_Control master_control_1 (
    .Opcode(instruction_fields_1_opcode), .subop(instruction_fields_1_subop),
    .Operation(master_control_1_operation), .setRegValue(master_control_1_setregvalue),
    .SetRegValue2(master_control_1_setregvalue2), .setRegValue3(master_control_1_setregvalue3),
    .WriteEn(master_control_1_writeen));
  Demultiplexer #(.select(2), .width(4), .enable("false")) demultiplexer_1 (
    .out0(demultiplexer_1_out0), .out1(demultiplexer_1_out1), .out2(demultiplexer_1_out2),
    .out3(demultiplexer_1_out3), .in(instruction_fields_1_opcode), .sel(master_control_1_operation));
  Data_Address_handler data_address_handler_1 (
    .rt(register_file_1_read_data_1), .Effective_Address(data_address_handler_1_effective_address));
  Multiplexer #(.width(16), .enable("false")) multiplexer_8 (
    .in0(register_file_1_read_data_1), .in1(multiplexer_4_out), .out(multiplexer_8_out),
    .sel(main_control_1_alusrc));
  Register #(.width(16)) register_2 (
    .D(register_file_1_read_data_0), .en(output_control_1_put),
    .Q({register_2_q_4, register_2_q_3, register_2_q_2, register_2_q}), .clk(clock_1_out));  // open: clr
  ALU alu_1 (
    .A(register_file_1_read_data_0), .B(multiplexer_8_out), .Operation(main_control_1_operation),
    .Result(alu_1_result));
  Jump_Handler jump_handler_1 (
    .PC_1(adder_1_out), .immediate(bit_extender_1_out), .rs(register_file_1_read_data_0),
    .Jump_Type(pc_control_1_jump_type), .PC_Value(jump_handler_1_pc_value), .rs_Value(jump_handler_1_rs_value));

  // Notes on the sheet:
  //   contents of rom_1 (hex, n*v repeats v):
  //   1fc1 2fff 1901 29ff 7800 1001 2013 dc18 1901 2955 7800 6000 2ffe 5dc1 7000 b024 21fe dc18 5dc0 2e02
  //   cc00
  //   mem2reg
  //   branch mux
  //   regVal
  //   extend mux
  //   regVal2
  //   regVal3
  //   jump mux
  //   Alu src
  //   Matthew Strayhorn
  //   mas583@pitt.edu
endmodule

module ALU (
  input  [15:0] A,
  input  [15:0] B,
  input  [1:0] Operation,
  output [15:0] Result
);

  wire [15:0] adder_1_out, and_1_out, nor_1_out, subtractor_1_out;

  Adder #(.width(16)) adder_1 (.a(A), .b(B), .out(adder_1_out), .cin(1'b0));  // open: cout
  Subtractor #(.width(16)) subtractor_1 (.a(A), .b(B), .out(subtractor_1_out), .bin(1'b0));  // open: bout
  assign nor_1_out = ~(A | B);  // NOR_Gate nor_1, 16 bits wide
  assign and_1_out = A & B;  // AND_Gate and_1, 16 bits wide
  Multiplexer #(.select(2), .width(16), .enable("false")) multiplexer_1 (
    .in0(adder_1_out), .in1(subtractor_1_out), .in2(nor_1_out), .in3(and_1_out), .out(Result), .sel(Operation));
endmodule

module Register_File (
  input  [2:0] Read_Register_0,
  input  [2:0] Read_Register_1,
  input  Clock,
  input  Write_Enable,
  input  [15:0] Write_Data,
  input  [2:0] Write_Register,
  output [15:0] Read_Data_0,
  output [15:0] Read_Data_1
);

  wire and_1_out, and_2_out, and_3_out, and_4_out, and_5_out, and_6_out, and_7_out, and_8_out,
       decoder_1_out0, decoder_1_out1, decoder_1_out2, decoder_1_out3, decoder_1_out4, decoder_1_out5,
       decoder_1_out6, decoder_1_out7;
  wire [15:0] _0_q, _1_q, _2_q, _3_q, _4_q, _5_q, _6_q, _7_q;

  and and_1 (and_1_out, decoder_1_out3, Write_Enable);
  and and_2 (and_2_out, decoder_1_out2, Write_Enable);
  and and_3 (and_3_out, decoder_1_out1, Write_Enable);
  and and_4 (and_4_out, decoder_1_out0, Write_Enable);
  Register #(.width(16)) _0 (.D(Write_Data), .en(and_4_out), .Q(_0_q), .clk(Clock));  // open: clr
  Register #(.width(16)) _1 (.D(Write_Data), .en(and_3_out), .Q(_1_q), .clk(Clock));  // open: clr
  Register #(.width(16)) _2 (.D(Write_Data), .en(and_2_out), .Q(_2_q), .clk(Clock));  // open: clr
  Register #(.width(16)) _3 (.D(Write_Data), .en(and_1_out), .Q(_3_q), .clk(Clock));  // open: clr
  Register #(.width(16)) _4 (.D(Write_Data), .en(and_8_out), .Q(_4_q), .clk(Clock));  // open: clr
  Register #(.width(16)) _5 (.D(Write_Data), .en(and_7_out), .Q(_5_q), .clk(Clock));  // open: clr
  Register #(.width(16)) _6 (.D(Write_Data), .en(and_6_out), .Q(_6_q), .clk(Clock));  // open: clr
  Register #(.width(16)) _7 (.D(Write_Data), .en(and_5_out), .Q(_7_q), .clk(Clock));  // open: clr
  and and_5 (and_5_out, decoder_1_out7, Write_Enable);
  and and_6 (and_6_out, decoder_1_out6, Write_Enable);
  and and_7 (and_7_out, decoder_1_out5, Write_Enable);
  and and_8 (and_8_out, decoder_1_out4, Write_Enable);
  Multiplexer #(.select(3), .width(16)) multiplexer_1 (
    .in0(_0_q), .in1(_1_q), .in2(_2_q), .in3(_3_q), .in4(_4_q), .in5(_5_q), .in6(_6_q), .in7(_7_q),
    .out(Read_Data_0), .sel(Read_Register_0));  // open: en
  Multiplexer #(.select(3), .width(16)) multiplexer_2 (
    .in0(_0_q), .in1(_1_q), .in2(_2_q), .in3(_3_q), .in4(_4_q), .in5(_5_q), .in6(_6_q), .in7(_7_q),
    .out(Read_Data_1), .sel(Read_Register_1));  // open: en
  Decoder #(.select(3)) decoder_1 (
    .out0(decoder_1_out0), .out1(decoder_1_out1), .out2(decoder_1_out2), .out3(decoder_1_out3),
    .out4(decoder_1_out4), .out5(decoder_1_out5), .out6(decoder_1_out6), .out7(decoder_1_out7),
    .sel(Write_Register));  // open: en
endmodule

module Instruction_Fields (
  input  [15:0] Instruction,
  output SubOp,
  output [3:0] shamt,
  output [2:0] Rt,
  output [7:0] Immediate,
  output [2:0] Rs,
  output [3:0] Opcode
);


  assign Immediate = Instruction[8:1];
  assign Opcode = Instruction[15:12];
  assign Rs = Instruction[11:9];
  assign Rt = Instruction[8:6];
  assign shamt = Instruction[4:1];
  assign SubOp = Instruction[0];
endmodule

module Master_Control (
  input  [3:0] Opcode,
  input  subop,
  output [1:0] Operation,
  output setRegValue,
  output SetRegValue2,
  output setRegValue3,
  output WriteEn
);

  wire and_1_out, and_2_out, and_3_out, and_4_out, and_5_out, and_7_out, and_8_out, and_9_out, and_10_out,
       and_11_out, and_12_out, and_13_out, and_14_out, not_1_out, not_2_out, not_3_out, not_4_out, not_5_out,
       not_6_out, not_7_out, not_8_out, not_9_out, not_10_out, not_11_out, not_12_out, not_13_out,
       not_14_out, not_15_out, not_16_out, not_17_out, not_18_out, not_19_out, not_20_out, not_21_out;

  not not_1 (not_1_out, Opcode[2]);
  not not_2 (not_2_out, Opcode[0]);
  not not_3 (not_3_out, Opcode[1]);
  not not_4 (not_4_out, Opcode[3]);
  not not_5 (not_5_out, Opcode[2]);
  not not_6 (not_6_out, Opcode[1]);
  not not_7 (not_7_out, Opcode[3]);
  not not_8 (not_8_out, Opcode[2]);
  not not_9 (not_9_out, Opcode[3]);
  not not_10 (not_10_out, Opcode[1]);
  not not_11 (not_11_out, Opcode[0]);
  not not_12 (not_12_out, Opcode[3]);
  not not_13 (not_13_out, Opcode[1]);
  not not_14 (not_14_out, subop);
  not not_15 (not_15_out, Opcode[1]);
  and and_1 (and_1_out, not_1_out, not_2_out);
  and and_2 (and_2_out, not_3_out, Opcode[0]);
  and and_3 (and_3_out, Opcode[3], Opcode[0]);
  and and_4 (and_4_out, not_4_out, Opcode[2], Opcode[1]);
  and and_5 (and_5_out, Opcode[3], not_5_out);
  and and_6 (setRegValue3, Opcode[3], Opcode[2], not_6_out, Opcode[0]);
  and and_7 (and_7_out, not_7_out, not_8_out);
  and and_8 (and_8_out, not_9_out, not_10_out, not_11_out);
  and and_9 (and_9_out, not_12_out, not_13_out, not_14_out);
  and and_10 (and_10_out, Opcode[3], Opcode[2], not_15_out, Opcode[0]);
  not not_16 (not_16_out, Opcode[2]);
  not not_17 (not_17_out, Opcode[1]);
  not not_18 (not_18_out, Opcode[0]);
  not not_19 (not_19_out, Opcode[2]);
  not not_20 (not_20_out, Opcode[0]);
  not not_21 (not_21_out, Opcode[1]);
  or or_1 (setRegValue, and_1_out, and_2_out, and_3_out);
  or or_2 (SetRegValue2, and_4_out, and_5_out);
  or or_3 (WriteEn, and_7_out, and_8_out, and_9_out, and_10_out);
  and and_11 (and_11_out, not_16_out, Opcode[1], Opcode[0]);
  and and_12 (and_12_out, Opcode[2], not_17_out, not_18_out);
  and and_13 (and_13_out, not_19_out, not_20_out);
  and and_14 (and_14_out, not_21_out, Opcode[0]);
  or or_4 (Operation[1], and_11_out, and_12_out, Opcode[3]);
  or or_5 (Operation[0], and_13_out, and_14_out, Opcode[3]);
endmodule

module Main_Control (
  input  [3:0] Opcode,
  input  SubOp,
  output AluSrc,
  output [1:0] Operation,
  output Mem2Reg,
  output ExtendType,
  output MemRead,
  output MemWrite
);

  wire and_2_out, and_3_out, and_4_out, and_5_out, and_6_out, and_7_out, and_8_out, not_1_out, not_2_out,
       not_3_out, not_4_out, not_5_out, not_6_out, not_7_out, not_8_out, not_9_out, not_10_out, not_11_out;

  or or_1 (AluSrc, Opcode[1], Opcode[2]);
  not not_1 (not_1_out, Opcode[1]);
  not not_2 (not_2_out, Opcode[0]);
  not not_3 (not_3_out, Opcode[1]);
  not not_4 (not_4_out, Opcode[0]);
  not not_5 (not_5_out, SubOp);
  not not_6 (not_6_out, Opcode[2]);
  not not_7 (not_7_out, Opcode[3]);
  not not_8 (not_8_out, SubOp);
  not not_9 (not_9_out, SubOp);
  not not_10 (not_10_out, Opcode[3]);
  not not_11 (not_11_out, Opcode[1]);
  not not_12 (MemRead, SubOp);
  and and_1 (Operation[1], not_1_out, not_2_out);
  and and_2 (and_2_out, not_3_out, not_4_out, not_5_out);
  and and_3 (and_3_out, not_6_out, Opcode[0], SubOp);
  and and_4 (and_4_out, Opcode[1], Opcode[0], SubOp);
  and and_5 (and_5_out, Opcode[3], Opcode[0], SubOp);
  and and_6 (and_6_out, not_7_out, not_8_out);
  and and_7 (and_7_out, Opcode[2], not_9_out);
  and and_8 (and_8_out, not_10_out, Opcode[2], not_11_out, Opcode[0]);
  or or_2 (Operation[0], and_2_out, and_3_out, and_4_out, and_5_out);
  or or_3 (ExtendType, and_6_out, and_7_out, and_8_out);

  assign Mem2Reg = Opcode[2];
  assign MemWrite = SubOp;
endmodule

module PC_Control (
  input  [3:0] Opcode,
  output [1:0] Comparison,
  output Branch,
  output Jump,
  output [1:0] Jump_Type
);

  wire and_4_out, and_5_out, not_1_out, not_2_out, not_3_out, not_4_out;

  not not_1 (not_1_out, Opcode[1]);
  and and_1 (Comparison[0], Opcode[1], Opcode[0]);
  not not_2 (not_2_out, Opcode[2]);
  not not_3 (not_3_out, Opcode[1]);
  not not_4 (not_4_out, Opcode[0]);
  and and_2 (Comparison[1], not_1_out, Opcode[0]);
  and and_3 (Branch, Opcode[3], not_2_out);
  and and_4 (and_4_out, Opcode[3], Opcode[2], not_3_out);
  and and_5 (and_5_out, Opcode[3], Opcode[2], not_4_out);
  or or_1 (Jump, and_4_out, and_5_out);

  assign Jump_Type = Opcode[1:0];
endmodule

module Shift_Control (
  input  [3:0] Opcode,
  input  SubOp,
  output Direction,
  output RtOrShamt
);

  not not_1 (RtOrShamt, Opcode[1]);

  assign Direction = SubOp;
endmodule

module Output_Control (
  input  [3:0] Opcode,
  output Halt,
  output Put
);

  wire not_1_out, not_2_out, not_3_out;

  not not_1 (not_1_out, Opcode[2]);
  not not_2 (not_2_out, Opcode[1]);
  not not_3 (not_3_out, Opcode[3]);
  or or_1 (Halt, not_1_out, not_2_out, Opcode[0], Opcode[3]);
  and and_1 (Put, not_3_out, Opcode[2], Opcode[1], Opcode[0]);
endmodule

module _16_to_8_bits (
  input  [15:0] \input ,
  output [7:0] Output
);


  assign Output = \input [7:0];
endmodule

module _16_to_4_bits (
  input  [15:0] \input ,
  output [3:0] rt
);


  assign rt = \input [3:0];
endmodule

module Shift_handler (
  input  [3:0] Shamt,
  input  [15:0] Rt,
  input  Rt_or_Shamt,
  input  Direction,
  input  [15:0] Input,
  output [15:0] Output
);

  wire [3:0] demultiplexer_1_out0, demultiplexer_1_out1, multiplexer_1_out, n16_to_4_bits_1_rt;
  wire [15:0] shifter_1_out, shifter_2_out;

  _16_to_4_bits u_16_to_4_bits_1 (.\input (Rt), .rt(n16_to_4_bits_1_rt));
  Multiplexer #(.width(4), .enable("false")) multiplexer_1 (
    .in0(Shamt), .in1(n16_to_4_bits_1_rt), .out(multiplexer_1_out), .sel(Rt_or_Shamt));
  Demultiplexer #(.width(4), .enable("false")) demultiplexer_1 (
    .out0(demultiplexer_1_out0), .out1(demultiplexer_1_out1), .in(multiplexer_1_out), .sel(Direction));
  Shifter #(.width(16)) shifter_1 (.in(Input), .\dist (demultiplexer_1_out0), .out(shifter_1_out));
  Shifter #(.width(16), .shift("lr")) shifter_2 (.in(Input), .\dist (demultiplexer_1_out1), .out(shifter_2_out));
  Multiplexer #(.width(16), .enable("false")) multiplexer_2 (
    .in0(shifter_1_out), .in1(shifter_2_out), .out(Output), .sel(Direction));
endmodule

module Branch_Handler (
  input  [7:0] RS,
  input  [1:0] Comparison,
  output Zero_Output
);

  wire comparator_1_eq, comparator_1_gt, comparator_1_lt;

  Comparator comparator_1 (.a(RS), .b({8{1'b0}}), .gt(comparator_1_gt), .eq(comparator_1_eq), .lt(comparator_1_lt));
  Multiplexer #(.select(2), .enable("false")) multiplexer_1 (
    .in0(comparator_1_gt), .in1(comparator_1_eq), .in2(comparator_1_lt), .out(Zero_Output), .sel(Comparison));  // open: in3
endmodule

module Jump_Handler (
  input  [7:0] PC_1,
  input  [15:0] immediate,
  input  [15:0] rs,
  input  [1:0] Jump_Type,
  output [7:0] PC_Value,
  output [15:0] rs_Value
);

  wire [7:0] n16_to_8_bits_1_output, n16_to_8_bits_2_output;

  _16_to_8_bits u_16_to_8_bits_1 (.\input (immediate), .Output(n16_to_8_bits_1_output));
  _16_to_8_bits u_16_to_8_bits_2 (.\input (rs), .Output(n16_to_8_bits_2_output));
  Multiplexer #(.select(2), .width(8), .enable("false")) multiplexer_1 (
    .in0(n16_to_8_bits_2_output), .in1(n16_to_8_bits_1_output), .in2(n16_to_8_bits_1_output), .out(PC_Value),
    .sel(Jump_Type));  // open: in3
  assign rs_Value = {{8{1'b0}}, PC_1};  // Bit_Extender bit_extender_1
endmodule

module Data_Address_handler (
  input  [15:0] rt,
  output [7:0] Effective_Address
);

  Bit_Extender #(.in_width(16), .out_width(8), .\type ("sign")) bit_extender_1 (.in(rt), .out(Effective_Address));
endmodule
