// Logisim project lab09part1-MAS583.circ as structural Verilog: 1 circuit, main circuit main
module main (
  input  A1,
  input  A0,
  input  B1,
  input  B0,
  output Y
);

  wire and_1_out, and_2_out, and_3_out, and_4_out, not_1_out, not_2_out, not_3_out, not_4_out, not_5_out,
       not_6_out, not_7_out, not_8_out;

  not not_1 (not_1_out, A1);
  not not_2 (not_2_out, A0);
  not not_3 (not_3_out, B0);
  not not_4 (not_4_out, A1);
  not not_5 (not_5_out, A0);
  not not_6 (not_6_out, B1);
  not not_7 (not_7_out, B0);
  not not_8 (not_8_out, B1);
  and and_1 (and_1_out, not_1_out, not_2_out, B1, not_3_out);
  and and_2 (and_2_out, not_4_out, A0, B1, B0);
  and and_3 (and_3_out, A1, not_5_out, not_6_out, not_7_out);
  and and_4 (and_4_out, A1, A0, not_8_out, B0);
  or or_1 (Y, and_1_out, and_2_out, and_3_out, and_4_out);
endmodule
