// Logisim project lab09part2-MAS583.circ as structural Verilog: 2 circuits, main circuit main
module main (
  output out_1,
  output out_2,
  output out_3,
  output out_4,
  output out_5,
  output out_6,
  output out_7,
  output out_8,
  output out_9,
  output out_10,
  output out_11,
  output out_12
);

  wire Batch_1_out, Batch_2_out, Batch_3_out, Batch_4_out, Batch_5_out, Batch_6_out, clock_1_out;

  Clock clock_1 (.out(clock_1_out));
  Button Batch_1 (.out(Batch_1_out));
  Button Batch_2 (.out(Batch_2_out));
  Button Batch_3 (.out(Batch_3_out));
  Button Batch_4 (.out(Batch_4_out));
  Button Batch_5 (.out(Batch_5_out));
  Button Batch_6 (.out(Batch_6_out));
  CookieWatcher cookiewatcher_1 (
    .Clock(clock_1_out), .BatchHandled(Batch_1_out), .CookiesBurnt(out_1), .CookiesDone(out_2));
  CookieWatcher cookiewatcher_2 (
    .Clock(clock_1_out), .BatchHandled(Batch_2_out), .CookiesBurnt(out_3), .CookiesDone(out_4));
  CookieWatcher cookiewatcher_3 (
    .Clock(clock_1_out), .BatchHandled(Batch_3_out), .CookiesBurnt(out_5), .CookiesDone(out_6));
  CookieWatcher cookiewatcher_4 (
    .Clock(clock_1_out), .BatchHandled(Batch_4_out), .CookiesBurnt(out_7), .CookiesDone(out_8));
  CookieWatcher cookiewatcher_5 (
    .Clock(clock_1_out), .BatchHandled(Batch_5_out), .CookiesBurnt(out_9), .CookiesDone(out_10));
  CookieWatcher cookiewatcher_6 (
    .Clock(clock_1_out), .BatchHandled(Batch_6_out), .CookiesBurnt(out_11), .CookiesDone(out_12));
endmodule

module CookieWatcher (
  input  Clock,
  input  BatchHandled,
  output CookiesBurnt,
  output CookiesDone
);

  wire [8:0] counter_1_q;

  Counter #(.width(10), .max('h3ff), .ongoal("stay")) counter_1 (
    .load(1'b0), .count(1'b1), .Q({CookiesDone, counter_1_q}), .clk(Clock), .clr(BatchHandled));  // open: D, carry
  and and_1 (CookiesBurnt, counter_1_q[8], CookiesDone);
endmodule
