// Logisim project lab10part1-MAS583.circ as structural Verilog: 1 circuit, main circuit main
module main (
  input  WriteEnable,
  input  [1:0] ReadRegister1,
  input  [1:0] ReadRegister2,
  input  [1:0] WriteRegister,
  input  [15:0] WriteData,
  output [15:0] ReadData1,
  output [15:0] ReadData2
);

  wire and_1_out, and_2_out, and_3_out, and_4_out, clock_1_out, decoder_1_out0, decoder_1_out1,
       decoder_1_out2, decoder_1_out3;
  wire [15:0] Register_1_q, Register_2_q, Register_3_q, Register_4_q;

  and and_1 (and_1_out, WriteEnable, decoder_1_out3);
  Clock clock_1 (.out(clock_1_out));
  Register #(.width(16)) Register_1 (.D(WriteData), .en(and_4_out), .Q(Register_1_q), .clk(clock_1_out));  // open: clr
  Register #(.width(16)) Register_2 (.D(WriteData), .en(and_3_out), .Q(Register_2_q), .clk(clock_1_out));  // open: clr
  Register #(.width(16)) Register_3 (.D(WriteData), .en(and_2_out), .Q(Register_3_q), .clk(clock_1_out));  // open: clr
  Register #(.width(16)) Register_4 (.D(WriteData), .en(and_1_out), .Q(Register_4_q), .clk(clock_1_out));  // open: clr
  and and_2 (and_2_out, WriteEnable, decoder_1_out2);
  and and_3 (and_3_out, WriteEnable, decoder_1_out1);
  and and_4 (and_4_out, WriteEnable, decoder_1_out0);
  Decoder #(.select(2)) decoder_1 (
    .out0(decoder_1_out0), .out1(decoder_1_out1), .out2(decoder_1_out2), .out3(decoder_1_out3),
    .sel(WriteRegister));  // open: en
  Multiplexer #(.select(2), .width(16), .enable("false")) multiplexer_1 (
    .in0(Register_1_q), .in1(Register_2_q), .in2(Register_3_q), .in3(Register_4_q), .out(ReadData1),
    .sel(ReadRegister1));
  Multiplexer #(.select(2), .width(16), .enable("false")) multiplexer_2 (
    .in0(Register_1_q), .in1(Register_2_q), .in2(Register_3_q), .in3(Register_4_q), .out(ReadData2),
    .sel(ReadRegister2));
endmodule
