// Logisim project lab10part2-MAS583.circ as structural Verilog: 1 circuit, main circuit main
module main (
);

  wire adder_1_cout, clock_1_out, j_k_ff_1_q, Reset_Data_Counter_out, Reset_PC_Counter_out;
  wire [3:0] adder_1_out, counter_1_q;
  wire [7:0] adder_2_out, counter_2_q, ram_1_data;

  Clock clock_1 (.out(clock_1_out));
  Counter #(.width(4), .max('hf), .ongoal("continue")) counter_1 (
    .D(adder_1_out), .Q(counter_1_q), .clk(clock_1_out), .clr(Reset_PC_Counter_out));  // open: load, count, carry
  Button Reset_PC_Counter (.out(Reset_PC_Counter_out));
  Adder #(.width(4)) adder_1 (.a(4'b0001), .b(counter_1_q), .out(adder_1_out), .cout(adder_1_cout));  // open: cin
  J_K_Flip_Flop j_k_ff_1 (
    .J(adder_1_cout), .clk(clock_1_out), .K(1'b0), .Q(j_k_ff_1_q));  // open: Qn, preset, en, reset
  RAM #(.addrWidth(4)) ram_1 (
    .addr(counter_1_q), .data(ram_1_data), .clk(clock_1_out), .ld(j_k_ff_1_q));  // open: sel, clr
  Adder adder_2 (.a(8'h1), .b(ram_1_data), .out(adder_2_out));  // open: cin, cout
  Counter #(.ongoal("continue")) counter_2 (
    .D(adder_2_out), .Q(counter_2_q), .clk(clock_1_out), .clr(Reset_Data_Counter_out));  // open: load, count, carry
  assign ram_1_data = 1'b1 ? counter_2_q : 8'bz;  // Controlled_Buffer controlled_buffer_1
  Button Reset_Data_Counter (.out(Reset_Data_Counter_out));
endmodule
